# Fritzing sketch BenchPilot_260715 (saved by Fritzing 0.9.6b)
circuit board: 5cm x 7cm
breadboards: 1

parts:
  R3 = Resistor [tolerance=±5% power=0.25 resistance=10k package=THT]
  R1 = Resistor [tolerance=±5% power=0.25 resistance=10k package=THT]
  R5 = Resistor [tolerance=±5% power=0.25 resistance=6.8k package=THT]
  R2 = Resistor [tolerance=±5% power=0.25 resistance=2.2k package=THT]
  R4 = Resistor [tolerance=±5% power=0.25 resistance=3.9k package=THT]
  U1 = Mini-360 DC-DC Buck converter [package=THT]
  R6 = Resistor [tolerance=±5% power=0.25 resistance=27k package=THT]
  Q1 = PNP-Transistor [part_number=BC557 package="TO92 [THT]"]
  Q2 = NPN-Transistor [part_number=BC547 package="TO92 [THT]"]
  GND = Header 1 [package=smtra-256-8-6]
  12V = Header 1 [package=smtra-256-8-6]
  SEATALK_DATA = Header 1 [package=smtra-256-8-6]
  5V = Header 1 [package=smtra-256-8-6]
  GND_2 = Header 1 [package=smtra-256-8-6]
  RX = Header 1 [package=smtra-256-8-6]
  ESP32_TX = Header 1 [package=smtra-256-8-6]

nets:
  N1: R3.Pin_0, ESP32_TX.1
  N2: R3.Pin_1, R4.Pin_0, Q2.B
  N3: R1.Pin_0, Q2.C, SEATALK_DATA.1
  N4: R1.Pin_1, R2.Pin_1, Q1.B
  N5: R5.Pin_0, R6.Pin_0, RX.1
  N6: R5.Pin_1, R4.Pin_1, U1.OUT-, Q2.E, GND_2.1
  N7: R2.Pin_0, U1.IN+, Q1.E, 12V.1
  N8: U1.IN-, GND.1
  N9: U1.OUT+, 5V.1
  N10: R6.Pin_1, Q1.C

notes:
  GND
  12V
  5V
  RX
  TX
  Bench
  ESP32
  SEATALK
  Pilot
  DATA
  version 15.7.2026

custom parts:
  Mini-360 DC-DC Buck converter: Mini-360 DC-DC Buck converter. Tiny buck step down voltage converter, input voltage 4.75 to 23V output 1 to 17V adjustable. Available from ebay and the like.
